# Fritzing sketch useless_box_schema (saved by Fritzing 0.8.7b)
circuit board: 8.46667cm x 5.64444cm
breadboards: 1

parts:
  Composant1 = Arduino Uno (Rev3) - ICSP
  S1 = Toggle Switch [package=THT]
  R1 = Resistor [tolerance=±5% resistance=220 package=THT]
  J1 = Basic Servo
  LED1 = LED - 5mm [color="Red (633nm)" package="5 mm [THT]"]
  R2 = Resistor [tolerance=±5% resistance=220 package=THT]
  VCC1 = Battery block 9V
  S2 = Toggle Switch [package=THT]

nets:
  GND: Composant1.GND, R1.Pin_0, J1.gnd, LED1.cathode, VCC1.-
  N1: Composant1.D9_PWM, J1.pulse
  N2: Composant1.D13/SCK, R2.Pin_1
  N3: Composant1.D2, S1.L1, R1.Pin_1
  5V: Composant1.5V, S1.COM, J1.vcc
  N4: Composant1.VIN, S2.COM
  N5: LED1.anode, R2.Pin_0
